// Logisim project 4-bit_Adder.circ as structural Verilog: 2 circuits, main circuit RCA4
module FA1 (
  input  Cin,
  input  Y,
  input  X,
  output Cout,
  output S
);

  wire and_1_out, and_2_out, xor_2_out;

  or or_1 (Cout, and_1_out, and_2_out);
  and and_1 (and_1_out, Y, X);
  and and_2 (and_2_out, Cin, xor_2_out);
  xor xor_1 (S, Cin, xor_2_out);
  xor xor_2 (xor_2_out, Y, X);

  // Notes on the sheet:
  //   输入引脚区
  //   输出引脚区
  //   注意：请勿对上面区域的内容做任何修改！只在下面区域进行电路设计
  //   S = X ^ Y ^ Cin
  //   1位全加器逻辑函数
  //   Cout = X Y + Cin (X ^ Y)
endmodule

module RCA4 (
  input  C0,
  input  [3:0] Y,
  input  [3:0] X,
  output C4,
  output [3:0] S,
  output Overflow
);

  wire fa1_2_cout, fa1_3_cout, fa1_4_cout;

  xor xor_1 (Overflow, fa1_2_cout, C4);
  // Probe on Y
  // Probe on X
  FA1 fa1_1 (.S(S[3]), .Cout(C4), .Cin(fa1_2_cout), .Y(X[3]), .X(Y[3]));
  FA1 fa1_2 (.S(S[2]), .Cout(fa1_2_cout), .Cin(fa1_3_cout), .Y(X[2]), .X(Y[2]));
  // Probe on S
  FA1 fa1_3 (.S(S[1]), .Cout(fa1_3_cout), .Cin(fa1_4_cout), .Y(X[1]), .X(Y[1]));
  FA1 fa1_4 (.S(S[0]), .Cout(fa1_4_cout), .Cin(C0), .Y(X[0]), .X(Y[0]));
  // Probe on X
  // Probe on Y
  // Probe on C0
  // Probe on S

  // Other names for the same wires on the sheet: OF = Overflow

  // Notes on the sheet:
  //   输入引脚区
  //   注意：请勿对上面区域的内容做任何修改！只在下面区域进行电路设计
  //   输出引脚区
  //   +
  //   =
endmodule
